# Fritzing sketch Schaltplan des Projekt (saved by Fritzing 1.0.2b)
breadboards: 1

parts:
  Bauteil1 = Arduino Mega 2560 (Rev3)
  Keypad4x2 = Keypad Membran 4x4
  Bauteil2 = Bluetooth HC-05 Macho
  Bauteil3 = Bluetooth HC-05 Macho
  ARDUINO_DUE1 = Arduino Due (Rev2b)
  J2 = Basic Servo

nets:
  N1: Bauteil1.D19/RX1, Bauteil3.TXD
  N2: Bauteil1.D18/TX1, Bauteil3.RXD
  N3: Bauteil1.D9_PWM, Keypad4x2.Pin1
  N4: Bauteil1.D8_PWM, Keypad4x2.Pin2
  3V3: Bauteil1.3V3, Bauteil3.VCC
  GND: Bauteil1.GND, Bauteil3.GND
  N5: Bauteil1.D2_PWM, Keypad4x2.Pin8
  N6: Bauteil1.D3_PWM, Keypad4x2.Pin7
  N7: Bauteil1.D4_PWM, Keypad4x2.Pin6
  N8: Bauteil1.D5_PWM, Keypad4x2.Pin5
  N9: Bauteil1.D6_PWM, Keypad4x2.Pin4
  N10: Bauteil1.D7_PWM, Keypad4x2.Pin3
  N11: Bauteil2.TXD, ARDUINO_DUE1.D19/RX1
  N12: Bauteil2.RXD, ARDUINO_DUE1.D18/TX1
  N13: Bauteil2.VCC, ARDUINO_DUE1.IOREF
  GND_2: Bauteil2.GND, ARDUINO_DUE1.GND, J2.gnd
  5V: ARDUINO_DUE1.5V, J2.vcc
  N14: ARDUINO_DUE1.D10_PWM/SS0, J2.pulse

notes:
  - VCC INTO 3.3V
  - 2 HC- 05 BLUETOOH MODULE
  - SERVO + INTO 5V

custom parts:
  Arduino Mega 2560 (Rev3): The Arduino Mega 2560 is a microcontroller board based on the ATmega2560 (datasheet). It has 54 digital input/output pins (of which 14 can be used as PWM outputs), 16 analog inputs, 4 UARTs (hardware serial ports), a 16 MHz crystal oscillator, a USB connection, a power jack, an ICSP header, and a reset button. It contains everything needed to support the microcontroller; simply connect it to a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
  Keypad Membran 4x4: Membrane Keypad 4x4 Matrix
